// Logisim project simpleRISC_reduced.circ as structural Verilog: 5 circuits, main circuit main
module main (
);

  wire ADD, CLK, CMP, EQ, GT, I, SUB, Write_En;
  wire [0:0] or_1_out;
  wire [3:0] ALU_Sel;
  wire [15:0] imm;
  wire [31:0] Add_Sub_data, adder_1_out, Cmp_data, data_2, ex_imm, h_mod_ext, PC, Reg_w_data, rs1_data,
       rs2_data, signed_ext, zero_ext;
  wire [31:16] INSTRUCTION;

  Clock clock_1 (.out(CLK));
  Comparator #(.width(5)) comparator_1 (.a(INSTRUCTION[31:27]), .b({5{1'b0}}), .eq(ADD));  // open: gt, lt
  Comparator #(.width(5)) comparator_2 (.a(INSTRUCTION[31:27]), .b(5'b00001), .eq(SUB));  // open: gt, lt
  Comparator #(.width(5)) comparator_3 (.a(INSTRUCTION[31:27]), .b(5'b00101), .eq(CMP));  // open: gt, lt
  Comparator #(.width(32)) comparator_4 (.a(rs1_data), .b(rs2_data), .gt(GT), .eq(EQ));  // open: lt
  Multiplexer #(.select(2), .width(32)) multiplexer_1 (
    .in1(Add_Sub_data), .in2(Cmp_data), .out(Reg_w_data), .sel({CMP, or_1_out[0]}));  // open: in0, in3
  IMEM imem_1 (.IMEM_ADDR(PC), .INSTRUCTION({INSTRUCTION[31:27], I, INSTRUCTION[25:16], imm}));
  // LedBar #(.inputtype("row"), .matrixcols(32)) ledbar_1: pin names not known; wires that end beside it: INSTRUCTION[31:27], Reg_w_data
  or or_1 (or_1_out[0], ADD, SUB);
  Register #(.width(32)) register_1 (.D(adder_1_out), .en(CLK), .clk(CLK), .Q(PC));  // open: clr
  Adder #(.width(32)) adder_1 (.a(PC), .b(32'h4), .out(adder_1_out));  // open: cin, cout
  LedBar #(.matrixcols(32)) ledbar_2 (
    .led0(INSTRUCTION[31]), .led1(INSTRUCTION[30]), .led2(INSTRUCTION[29]), .led3(INSTRUCTION[28]),
    .led4(INSTRUCTION[27]), .led5(I), .led6(INSTRUCTION[25]), .led7(INSTRUCTION[24]), .led8(INSTRUCTION[23]),
    .led9(INSTRUCTION[22]), .led10(INSTRUCTION[21]), .led11(INSTRUCTION[20]), .led12(INSTRUCTION[19]),
    .led13(INSTRUCTION[18]), .led14(INSTRUCTION[17]), .led15(INSTRUCTION[16]), .led16(imm[15]),
    .led17(imm[14]), .led18(imm[13]), .led19(imm[12]), .led20(imm[11]), .led21(imm[10]), .led22(imm[9]),
    .led23(imm[8]), .led24(imm[7]), .led25(imm[6]), .led26(imm[5]), .led27(imm[4]), .led28(imm[3]),
    .led29(imm[2]), .led30(imm[1]), .led31(imm[0]));
  REGFILE regfile_1 (
    .rs1(INSTRUCTION[21:18]), .rs2({INSTRUCTION[17:16], imm[15:14]}), .rd(INSTRUCTION[25:22]),
    .REG_W_DATA(Reg_w_data), .WRITE_EN(Write_En), .CLK(CLK), .rs1_data(rs1_data), .rs2_data(rs2_data));
  ALU alu_1 (.ALU_X(rs1_data), .ALU_Y(data_2), .ALU_OP(ALU_Sel), .ALU_RESULT(Add_Sub_data));  // open: ALU_IS_EQ
  or or_2 (Write_En, ADD, CMP, SUB);
  LedBar #(.matrixcols(32)) ledbar_3 (
    .led0(rs1_data[31]), .led1(rs1_data[30]), .led2(rs1_data[29]), .led3(rs1_data[28]), .led4(rs1_data[27]),
    .led5(rs1_data[26]), .led6(rs1_data[25]), .led7(rs1_data[24]), .led8(rs1_data[23]), .led9(rs1_data[22]),
    .led10(rs1_data[21]), .led11(rs1_data[20]), .led12(rs1_data[19]), .led13(rs1_data[18]),
    .led14(rs1_data[17]), .led15(rs1_data[16]), .led16(rs1_data[15]), .led17(rs1_data[14]),
    .led18(rs1_data[13]), .led19(rs1_data[12]), .led20(rs1_data[11]), .led21(rs1_data[10]),
    .led22(rs1_data[9]), .led23(rs1_data[8]), .led24(rs1_data[7]), .led25(rs1_data[6]), .led26(rs1_data[5]),
    .led27(rs1_data[4]), .led28(rs1_data[3]), .led29(rs1_data[2]), .led30(rs1_data[1]), .led31(rs1_data[0]));
  LedBar #(.matrixcols(32)) ledbar_4 (
    .led0(rs2_data[31]), .led1(rs2_data[30]), .led2(rs2_data[29]), .led3(rs2_data[28]), .led4(rs2_data[27]),
    .led5(rs2_data[26]), .led6(rs2_data[25]), .led7(rs2_data[24]), .led8(rs2_data[23]), .led9(rs2_data[22]),
    .led10(rs2_data[21]), .led11(rs2_data[20]), .led12(rs2_data[19]), .led13(rs2_data[18]),
    .led14(rs2_data[17]), .led15(rs2_data[16]), .led16(rs2_data[15]), .led17(rs2_data[14]),
    .led18(rs2_data[13]), .led19(rs2_data[12]), .led20(rs2_data[11]), .led21(rs2_data[10]),
    .led22(rs2_data[9]), .led23(rs2_data[8]), .led24(rs2_data[7]), .led25(rs2_data[6]), .led26(rs2_data[5]),
    .led27(rs2_data[4]), .led28(rs2_data[3]), .led29(rs2_data[2]), .led30(rs2_data[1]), .led31(rs2_data[0]));
  Multiplexer #(.select(2), .width(4)) multiplexer_2 (
    .in1(4'b0000), .in2(4'b0001), .out(ALU_Sel), .sel({SUB, ADD}));  // open: in0, in3
  // LedBar #(.inputtype("row"), .matrixcols(32)) ledbar_5: pin names not known; wires that end beside it: Add_Sub_data
  Multiplexer #(.select(2), .width(32)) multiplexer_3 (
    .in1(32'h1), .in2({32{1'b0}}), .out(Cmp_data), .sel({EQ, GT}));  // open: in0, in3
  Multiplexer #(.width(32)) multiplexer_4 (.in0(rs2_data), .in1(ex_imm), .out(data_2), .sel(I));
  Shifter #(.width(32)) shifter_1 (.in(zero_ext), .\dist (5'b10000), .out(h_mod_ext));
  assign zero_ext = {{16{1'b0}}, imm};  // Bit_Extender bit_extender_1
  assign signed_ext = {{16{imm[15]}}, imm};  // Bit_Extender bit_extender_2
  Multiplexer #(.select(2), .width(32)) multiplexer_5 (
    .in0(zero_ext), .in1(signed_ext), .in2(h_mod_ext), .out(ex_imm), .sel(INSTRUCTION[17:16]));  // open: in3

  // Other names for the same wires on the sheet: INSTRUCTION (some bits) = {I, imm};
  //   rs2[3:0] = {INSTRUCTION[17:16], imm[15:14]}; m[1:0] = INSTRUCTION[17:16]; rs1[3:0] = INSTRUCTION[21:18];
  //   rd[3:0] = INSTRUCTION[25:22]; op[4:0] = INSTRUCTION[31:27]
endmodule

module DMEM (
  input  [31:0] DMEM_ADDR,
  input  DMEM_W_EN,
  input  CLK,
  input  [31:0] DMEM_W_DATA,
  output [31:0] DMEM_R_DATA
);

  RAM #(.addrWidth(10), .dataWidth(32), .enables("line")) ram_1 (
    .addr(DMEM_ADDR[9:0]), .we(DMEM_W_EN), .clk(CLK), .din(DMEM_W_DATA), .dout(DMEM_R_DATA));

  // Other names for the same wires on the sheet: DMEM_READ_DATA[31:0] = DMEM_R_DATA;
  //   DMEM_WRITE_DATA[31:0] = DMEM_W_DATA; DMEM_WRITE_EN = DMEM_W_EN
endmodule

module IMEM (
  input  [31:0] IMEM_ADDR,
  output [31:0] INSTRUCTION
);

  // ROM #(.addrWidth(10), .line("quad")) rom_1: pin names not known; wires that end beside it: IMEM_ADDR[9:0], INSTRUCTION[7:0], INSTRUCTION[15:8], INSTRUCTION[23:16], INSTRUCTION[31:24]

  // Notes on the sheet:
  //   contents of rom_1 (hex, n*v repeats v):
  //   3 0 48 4 3 0 c4 4 2 6*1 3
endmodule

module REGFILE (
  input  [3:0] rs1,
  input  [3:0] rs2,
  input  [3:0] rd,
  input  [31:0] REG_W_DATA,
  input  WRITE_EN,
  input  CLK,
  output [31:0] rs1_data,
  output [31:0] rs2_data
);

  wire WE_1, WE_2, WE_3, WE_4, WE_5, WE_6, WE_7, WE_8, WE_9, WE_10, WE_11, WE_12, WE_13, WE_14, WE_15, WE_16,
       WE_17, WE_18, WE_19, WE_20, WE_21, WE_22, WE_23, WE_24, WE_25, WE_26, WE_27, WE_28, WE_29, WE_30,
       WE_31;
  wire [31:0] in_r1, in_r2, in_r3, in_r4, in_r5, in_r6, in_r7, in_r8, in_r9, in_r10, in_r11, in_r12, in_r13,
       in_r14, in_r15, in_r16, in_r17, in_r18, in_r19, in_r20, in_r21, in_r22, in_r23, in_r24, in_r25,
       in_r26, in_r27, in_r28, in_r29, in_r30, in_r31, out_r1, out_r2, out_r3, out_r4, out_r5, out_r6,
       out_r7, out_r8, out_r9, out_r10, out_r11, out_r12, out_r13, out_r14, out_r15, out_r16, out_r17,
       out_r18, out_r19, out_r20, out_r21, out_r22, out_r23, out_r24, out_r25, out_r26, out_r27, out_r28,
       out_r29, out_r30, out_r31;

  Register #(.width(32)) r1 (.D(in_r1), .en(WE_1), .clk(CLK), .Q(out_r1));  // open: clr
  Register #(.width(32)) register_1 (.D(in_r9), .en(WE_9), .clk(CLK), .Q(out_r9));  // open: clr
  Register #(.width(32)) register_2 (.D(in_r17), .en(WE_17), .clk(CLK), .Q(out_r17));  // open: clr
  Register #(.width(32)) register_3 (.D(in_r25), .en(WE_25), .clk(CLK), .Q(out_r25));  // open: clr
  Multiplexer #(.select(5), .width(32)) multiplexer_1 (
    .in0({32{1'b0}}), .in1(out_r1), .in2(out_r2), .in3(out_r3), .in4(out_r4), .in5(out_r5), .in6(out_r6),
    .in7(out_r7), .in8(out_r8), .in9(out_r9), .in10(out_r10), .in11(out_r11), .in12(out_r12), .in13(out_r13),
    .in14(out_r14), .in15(out_r15), .in16(out_r16), .in17(out_r17), .in18(out_r18), .in19(out_r19),
    .in20(out_r20), .in21(out_r21), .in22(out_r22), .in23(out_r23), .in24(out_r24), .in25(out_r25),
    .in26(out_r26), .in27(out_r27), .in28(out_r28), .in29(out_r29), .in30(out_r30), .in31(out_r31),
    .out(rs1_data), .sel({1'b0, rs1}));
  Register #(.width(32)) register_4 (.D(in_r2), .en(WE_2), .clk(CLK), .Q(out_r2));  // open: clr
  Register #(.width(32)) register_5 (.D(in_r10), .en(WE_10), .clk(CLK), .Q(out_r10));  // open: clr
  Register #(.width(32)) register_6 (.D(in_r18), .en(WE_18), .clk(CLK), .Q(out_r18));  // open: clr
  Register #(.width(32)) register_7 (.D(in_r26), .en(WE_26), .clk(CLK), .Q(out_r26));  // open: clr
  Register #(.width(32)) register_8 (.D(in_r3), .en(WE_3), .clk(CLK), .Q(out_r3));  // open: clr
  Register #(.width(32)) register_9 (.D(in_r11), .en(WE_11), .clk(CLK), .Q(out_r11));  // open: clr
  Register #(.width(32)) register_10 (.D(in_r19), .en(WE_19), .clk(CLK), .Q(out_r19));  // open: clr
  Register #(.width(32)) register_11 (.D(in_r27), .en(WE_27), .clk(CLK), .Q(out_r27));  // open: clr
  Multiplexer #(.select(5), .width(32)) multiplexer_2 (
    .in0({32{1'b0}}), .in1(out_r1), .in2(out_r2), .in3(out_r3), .in4(out_r4), .in5(out_r5), .in6(out_r6),
    .in7(out_r7), .in8(out_r8), .in9(out_r9), .in10(out_r10), .in11(out_r11), .in12(out_r12), .in13(out_r13),
    .in14(out_r14), .in15(out_r15), .in16(out_r16), .in17(out_r17), .in18(out_r18), .in19(out_r19),
    .in20(out_r20), .in21(out_r21), .in22(out_r22), .in23(out_r23), .in24(out_r24), .in25(out_r25),
    .in26(out_r26), .in27(out_r27), .in28(out_r28), .in29(out_r29), .in30(out_r30), .in31(out_r31),
    .out(rs2_data), .sel({1'b0, rs2}));
  Register #(.width(32)) register_12 (.D(in_r4), .en(WE_4), .clk(CLK), .Q(out_r4));  // open: clr
  Register #(.width(32)) register_13 (.D(in_r12), .en(WE_12), .clk(CLK), .Q(out_r12));  // open: clr
  Register #(.width(32)) register_14 (.D(in_r20), .en(WE_20), .clk(CLK), .Q(out_r20));  // open: clr
  Register #(.width(32)) register_15 (.D(in_r28), .en(WE_28), .clk(CLK), .Q(out_r28));  // open: clr
  Demultiplexer #(.enable("true"), .select(5), .width(32)) demultiplexer_1 (
    .out1(in_r1), .out2(in_r2), .out3(in_r3), .out4(in_r4), .out5(in_r5), .out6(in_r6), .out7(in_r7),
    .out8(in_r8), .out9(in_r9), .out10(in_r10), .out11(in_r11), .out12(in_r12), .out13(in_r13),
    .out14(in_r14), .out15(in_r15), .out16(in_r16), .out17(in_r17), .out18(in_r18), .out19(in_r19),
    .out20(in_r20), .out21(in_r21), .out22(in_r22), .out23(in_r23), .out24(in_r24), .out25(in_r25),
    .out26(in_r26), .out27(in_r27), .out28(in_r28), .out29(in_r29), .out30(in_r30), .out31(in_r31),
    .in(REG_W_DATA), .sel({1'b0, rd}), .en(WRITE_EN));  // open: out0
  Register #(.width(32)) register_16 (.D(in_r5), .en(WE_5), .clk(CLK), .Q(out_r5));  // open: clr
  Register #(.width(32)) register_17 (.D(in_r13), .en(WE_13), .clk(CLK), .Q(out_r13));  // open: clr
  Register #(.width(32)) register_18 (.D(in_r21), .en(WE_21), .clk(CLK), .Q(out_r21));  // open: clr
  Register #(.width(32)) register_19 (.D(in_r29), .en(WE_29), .clk(CLK), .Q(out_r29));  // open: clr
  Register #(.width(32)) register_20 (.D(in_r6), .en(WE_6), .clk(CLK), .Q(out_r6));  // open: clr
  Register #(.width(32)) register_21 (.D(in_r14), .en(WE_14), .clk(CLK), .Q(out_r14));  // open: clr
  Register #(.width(32)) register_22 (.D(in_r22), .en(WE_22), .clk(CLK), .Q(out_r22));  // open: clr
  Register #(.width(32)) register_23 (.D(in_r30), .en(WE_30), .clk(CLK), .Q(out_r30));  // open: clr
  Decoder #(.select(5)) decoder_1 (
    .out1(WE_1), .out2(WE_2), .out3(WE_3), .out4(WE_4), .out5(WE_5), .out6(WE_6), .out7(WE_7), .out8(WE_8),
    .out9(WE_9), .out10(WE_10), .out11(WE_11), .out12(WE_12), .out13(WE_13), .out14(WE_14), .out15(WE_15),
    .out16(WE_16), .out17(WE_17), .out18(WE_18), .out19(WE_19), .out20(WE_20), .out21(WE_21), .out22(WE_22),
    .out23(WE_23), .out24(WE_24), .out25(WE_25), .out26(WE_26), .out27(WE_27), .out28(WE_28), .out29(WE_29),
    .out30(WE_30), .out31(WE_31), .sel({1'b0, rd}), .en(WRITE_EN));  // open: out0
  Register #(.width(32)) register_24 (.D(in_r7), .en(WE_7), .clk(CLK), .Q(out_r7));  // open: clr
  Register #(.width(32)) register_25 (.D(in_r15), .en(WE_15), .clk(CLK), .Q(out_r15));  // open: clr
  Register #(.width(32)) register_26 (.D(in_r23), .en(WE_23), .clk(CLK), .Q(out_r23));  // open: clr
  Register #(.width(32)) register_27 (.D(in_r31), .en(WE_31), .clk(CLK), .Q(out_r31));  // open: clr
  Register #(.width(32)) register_28 (.D(in_r8), .en(WE_8), .clk(CLK), .Q(out_r8));  // open: clr
  Register #(.width(32)) register_29 (.D(in_r16), .en(WE_16), .clk(CLK), .Q(out_r16));  // open: clr
  Register #(.width(32)) register_30 (.D(in_r24), .en(WE_24), .clk(CLK), .Q(out_r24));  // open: clr

  // Other names for the same wires on the sheet: reg1[3:0] = rs1; reg1_data[31:0] = rs1_data; reg2[3:0] = rs2;
  //   reg2_data[31:0] = rs2_data; reg_write[3:0] = rd; reg_write_data[31:0] = REG_W_DATA; WE = WRITE_EN

  // Notes on the sheet:
  //   Outputs
  //   I/O
  //   Inputs
  //   Register Reading
  //   Register Writing
endmodule

module ALU (
  input  [31:0] ALU_X,
  input  [31:0] ALU_Y,
  input  [3:0] ALU_OP,
  output [31:0] ALU_RESULT,
  output ALU_IS_EQ
);

  wire comparator_1_lt;
  wire [31:0] o_add, o_and, o_div, o_mul, o_mulh, o_or, o_rem, o_sll, o_slt, o_srl, o_sub, o_xor;

  Multiplexer #(.select(4), .width(32)) multiplexer_1 (
    .in0(o_add), .in1(o_sub), .in2(o_and), .in3(o_or), .in4(o_xor), .in5(o_sll), .in6(o_srl), .in7(o_mul),
    .in8(o_mulh), .in9(o_div), .in10(o_rem), .in11(o_slt), .out(ALU_RESULT), .sel(ALU_OP));  // open: in12, in13, in14, in15
  Adder #(.width(32)) adder_1 (.a(ALU_X), .b(ALU_Y), .out(o_add));  // open: cin, cout
  Subtractor #(.width(32)) subtractor_1 (.a(ALU_X), .b(ALU_Y), .out(o_sub));  // open: bin, bout
  assign o_and = ALU_X & ALU_Y;  // AND_Gate and_1, 32 bits wide
  assign o_or = ALU_X | ALU_Y;  // OR_Gate or_1, 32 bits wide
  assign o_xor = ALU_X ^ ALU_Y;  // XOR_Gate xor_1, 32 bits wide
  Shifter #(.width(32)) shifter_1 (.in(ALU_X), .\dist (ALU_Y[4:0]), .out(o_sll));
  Comparator #(.width(32)) comparator_1 (.a(ALU_X), .b(ALU_Y), .lt(comparator_1_lt));  // open: gt, eq
  Shifter #(.shift("lr"), .width(32)) shifter_2 (.in(ALU_X), .\dist (ALU_Y[4:0]), .out(o_srl));
  Multiplier #(.width(32)) multiplier_1 (.a(ALU_X), .b(ALU_Y), .out(o_mul));  // open: cin, cout
  Multiplier #(.width(32)) multiplier_2 (.a(ALU_X), .b(ALU_Y), .cout(o_mulh));  // open: out, cin
  Divider #(.width(32)) divider_1 (.a(ALU_X), .b(ALU_Y), .out(o_div));  // open: upper, rem
  Divider #(.width(32)) divider_2 (.a(ALU_X), .b(ALU_Y), .rem(o_rem));  // open: out, upper
  Comparator #(.width(32)) comparator_2 (.a(ALU_X), .b(ALU_Y), .eq(ALU_IS_EQ));  // open: gt, lt
  Bit_Extender #(.in_width(1), .out_width(32)) bit_extender_1 (.out(o_slt));  // open: in

  // Other names for the same wires on the sheet: isEqual = ALU_IS_EQ; OP[3:0] = ALU_OP; result[31:0] = ALU_RESULT;
  //   X[31:0] = ALU_X; Y[31:0] = ALU_Y

  // Notes on the sheet:
  //   Outputs
  //   I/O
  //   Operation Selection
  //   Inputs
  //   Operations
endmodule
